# Fritzing sketch Testador_DS18B20 (saved by Fritzing 0.9.6b)

parts:
  A1 = Waveshare rp2040-zero tht [package=THT]
  Squix1 = OLED 0.96" 128x64 I2C SSD1306
  R1 = Resistor [tolerance=±5% power=0.25 resistance=470 package=THT]
  R2 = Resistor [tolerance=±5% power=0.25 resistance=4.7k package=THT]
  S1 = Adafruit 3104 lighted pushbutton [package=THT]
  J1 = Camdenboss CTB0158-3 [part_number=CTB0158-3 package=THT]

nets:
  N1: A1.Pin_2, Squix1.GND, S1.pin_2, S1.pin_5, S1.pin_1, J1.pin3
  N2: A1.Pin_3, Squix1.VCC
  N3: A1.Pin_6, R2.Pin_0, J1.pin2
  N4: A1.Pin_7, R2.Pin_1, J1.pin1
  N5: A1.Pin_8, S1.pin_4
  N6: A1.Pin_9, R1.Pin_0
  N7: A1.Pin_16, Squix1.SCL
  N8: A1.Pin_17, Squix1.SCA
  N9: R1.Pin_1, S1.pin_6

custom parts:
  Waveshare rp2040-zero tht: .RP2040-Zero, A Low-Cost, High-Performance Pico-Like MCU Board Based On Raspberry Pi Microcontroller RP2040. This varant is THT without the extra connections.
  Adafruit 3104 lighted pushbutton: This Mini Illuminated Momentary Power Button it an adorable breadboard-friendly tactile switch that has a built-in LED. It provides a simple way to add a tactile switch and a colorful universal power symbol to your project.
