# Fritzing sketch Testador_DS18B20_Pico (saved by Fritzing 0.9.6b)
breadboards: 1

parts:
  R1 = Resistor [tolerance=±5% power=0.25 resistance=470 package=THT]
  R2 = Resistor [tolerance=±5% power=0.25 resistance=4.7k package=THT]
  J1 = Camdenboss CTB0158-3 [part_number=CTB0158-3 package=THT]
  S1 = Pushbutton [package="[THT]"]
  LED2 = RGB LED (com. cathode, rgb) [package="5 mm [THT]"]
  Mod2 = Raspberry Pi Pico
  Squix2 = OLED 0.96" 128x64 I2C SSD1306
  R3 = Resistor [tolerance=±5% power=0.25 resistance=470 package=THT]
  R4 = Resistor [tolerance=±5% power=0.25 resistance=470 package=THT]

nets:
  N1: R1.Pin_0, LED2.red_anode
  N2: R1.Pin_1, Mod2.pin_20
  N3: R2.Pin_0, J1.pin3, Mod2.pin_32
  N4: R2.Pin_1, J1.pin2, Mod2.pin_31
  N5: J1.pin1, S1.Pin_3, S1.Pin_4, LED2.common_cathode, Mod2.pin_3, Mod2.pin_8, Mod2.pin_13, Mod2.pin_18, Mod2.pin_21, Mod2.pin_23, Mod2.pin_28, Mod2.pin_33, Mod2.pin_38, Squix2.GND
  N6: S1.Pin_1, S1.Pin_2
  N7: LED2.green_anode, R3.Pin_0
  N8: LED2.blue_anode, R4.Pin_0
  N9: Mod2.pin_9, Squix2.SCA
  N10: Mod2.pin_10, Squix2.SCL
  N11: Mod2.pin_17, R4.Pin_1
  N12: Mod2.pin_19, R3.Pin_1
  N13: Mod2.pin_36, Squix2.VCC

custom parts:
  Raspberry Pi Pico: Raspberry Pi Pico. Based around the RP2040 microcontroller the Pico is a low cost microcontroller device bringing Raspberry Pi quality, cost, and easy of use to the microcontroller space. Jan 2021, Split part in to two versions: tht (this one) and SMD. This one will drill holes for a .1 in header in pcb to allow plugging in the module as well as providing pads to solder the module to the top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
